// Logisim project Ejercicio 3.4.circ as structural Verilog: 2 circuits, main circuit main
module main (
);

  Control_Unit control_unit_1 ();  // open: RM, WM, OPC
endmodule

module Control_Unit (
  input  [2:0] OPC,
  output RM,
  output WM
);

  wire and_1_out, and_2_out, not_1_out, not_2_out, not_3_out, not_4_out, not_5_out;

  not not_1 (not_1_out, OPC[2]);
  not not_2 (not_2_out, OPC[0]);
  not not_3 (not_3_out, OPC[2]);
  not not_4 (not_4_out, OPC[2]);
  not not_5 (not_5_out, OPC[1]);
  and and_1 (and_1_out, not_1_out, not_2_out);
  or or_1 (RM, and_1_out, and_2_out);
  and and_2 (and_2_out, not_3_out, OPC[1]);
  and and_3 (WM, not_4_out, not_5_out, OPC[0]);
endmodule
