// Logisim project SumaCuadrados.circ as structural Verilog: 2 circuits, main circuit main
module main (
  input  [2:0] n,
  output [7:0] SCn
);

  wire Reset_out, suma_cuadrados_1_halt;

  Button Reset (.out(Reset_out));
  LED Halt (.in(suma_cuadrados_1_halt));
  suma_cuadrados suma_cuadrados_1 (.n(n), .Reset(Reset_out), .Halt(suma_cuadrados_1_halt), .SCn(SCn));
endmodule

module suma_cuadrados (
  input  [2:0] n,
  input  Reset,
  output Halt,
  output [7:0] SCn
);

  wire CLK_out, comparator_1_eq, comparator_1_gt, or_1_out;
  wire [3:0] bit_extender_1_out, counter_1_q;
  wire [7:0] adder_1_out, bit_extender_2_out, multiplier_1_out;

  Clock CLK (.out(CLK_out));
  Counter #(.width(4), .max('h8), .ongoal("stay")) counter_1 (
    .Q(counter_1_q), .clk(CLK_out), .clr(Reset));  // open: load, D, count, carry
  assign bit_extender_1_out = {{1{1'b0}}, n};  // Bit_Extender bit_extender_1
  assign bit_extender_2_out = {{4{1'b0}}, counter_1_q};  // Bit_Extender bit_extender_2
  Register register_1 (.D(adder_1_out), .en(or_1_out), .Q(SCn), .clk(CLK_out), .clr(Reset));
  Comparator #(.width(4), .mode("unsigned")) comparator_1 (
    .a(bit_extender_1_out), .b(counter_1_q), .gt(comparator_1_gt), .eq(comparator_1_eq), .lt(Halt));
  Multiplier multiplier_1 (.a(bit_extender_2_out), .b(bit_extender_2_out), .out(multiplier_1_out));  // open: cin, cout
  or or_1 (or_1_out, comparator_1_eq, comparator_1_gt);
  Adder adder_1 (.a(SCn), .b(multiplier_1_out), .out(adder_1_out));  // open: cin, cout

  // Notes on the sheet:
  //   Halt: pull=up
endmodule
