// Logisim project HPMIPS.circ as structural Verilog: 9 circuits, main circuit TG00MIPS
module TG00MIPS (
);

  wire CLK_out, mips_1_halt, stopclk_1_clkout;

  Clock #(.highDuration(2), .lowDuration(2)) CLK (.out(CLK_out));
  StopClk stopclk_1 (.halt(mips_1_halt), .clkin(CLK_out), .clkout(stopclk_1_clkout));
  MIPS mips_1 (.clk(stopclk_1_clkout), .reset(1'b0), .halt(mips_1_halt));
endmodule

// clk
module MIPS (
  input  clk,
  input  reset,
  output halt
);

  wire and_1_out, FB, FC, jump, MpxR, RM, WM, WR, Z;
  wire [1:0] AluOp;
  wire [3:0] control_alu_1_out;
  wire [4:0] multiplexer_2_out, rd, rs, rt;
  wire [5:0] func, instdecoder_1_ib31_26__opc;
  wire [15:0] imm;
  wire [25:0] addr;
  wire [31:0] dPC, immExt, instruction_memory_1_instruction, memres, multiplexer_1_out, multiplexer_3_out,
       multiplexer_4_out, multiplexer_5_out, PC, PC_q, register_file_1_read_data_1,
       register_file_1_read_data_2, res, shifter_1_out;

  Multiplexer #(.width(32), .enable("false")) multiplexer_1 (
    .in0(multiplexer_3_out), .in1(dPC), .out(multiplexer_1_out), .sel(and_1_out));
  Register #(.width(32)) u_PC (.D(multiplexer_1_out), .Q(PC_q), .clk(clk));  // open: en, clr
  Multiplexer #(.width(5), .enable("false")) multiplexer_2 (.in0(rd), .in1(rt), .out(multiplexer_2_out), .sel(MpxR));
  Multiplexer #(.width(32)) multiplexer_3 (
    .in0(PC), .in1({PC[31:28], addr, 2'b00}), .out(multiplexer_3_out), .sel(jump));  // open: en
  Adder #(.width(32)) adder_1 (.a(32'h4), .b(PC_q), .out(PC));  // open: cin, cout
  Multiplexer #(.width(32), .enable("false")) multiplexer_4 (
    .in0(res), .in1(memres), .out(multiplexer_4_out), .sel(FC));
  and and_1 (and_1_out, Z, AluOp[0]);
  Instruction_memory instruction_memory_1 (.Read_address(PC_q), .Instruction(instruction_memory_1_instruction));
  // Probe on instruction_memory_1_instruction
  Register_file register_file_1 (
    .Read_Register_1(rs), .Read_Register_2(rt), .Write_Register(multiplexer_2_out),
    .Write_Data(multiplexer_4_out), .Read_Data_1(register_file_1_read_data_1),
    .Read_Data_2(register_file_1_read_data_2), .clk(clk), .reset(reset), .Write(WR));
  Data_Memory_32 data_memory_32_1 (
    .Address(res), .Write_Data(register_file_1_read_data_2), .Read_Data(memres), .Write(WM), .clk(clk),
    .reset(reset), .Read(RM));
  InstDecoder instdecoder_1 (
    .IB(instruction_memory_1_instruction), .IB31_26__opc(instdecoder_1_ib31_26__opc), .IB25_21__rs(rs),
    .IB20_16__rt(rt), .IB15_11__rd(rd), .IB5_0__func(func), .IB15_0__imm(imm), .IB25_0__addr(addr));
  Multiplexer #(.width(32), .enable("false")) multiplexer_5 (
    .in0(immExt), .in1(register_file_1_read_data_2), .out(multiplexer_5_out), .sel(FB));
  ControlUnit controlunit_1 (
    .JUMP(jump), .HALT(halt), .RM(RM), .FC(FC), .WM(WM), .OPC(instdecoder_1_ib31_26__opc), .MpxR(MpxR),
    .WR(WR), .FB(FB), .AluOp0(AluOp[0]), .AluOp1(AluOp[1]));
  Control_ALU control_alu_1 (.OpALU(AluOp), .funcion(func), .OUT(control_alu_1_out));
  ALU alu_1 (
    .A(register_file_1_read_data_1), .B(multiplexer_5_out), .Z(Z), .Result(res), .Operation(control_alu_1_out));
  assign immExt = {{16{imm[15]}}, imm};  // Bit_Extender bit_extender_1
  Shifter #(.width(32)) shifter_1 (.in(immExt), .\dist (5'b00010), .out(shifter_1_out));
  Adder #(.width(32)) adder_2 (.a(PC), .b(shifter_1_out), .out(dPC));  // open: cin, cout
endmodule

module Register_file (
  input  clk,
  input  reset,
  input  [4:0] Read_Register_1,
  input  [4:0] Read_Register_2,
  input  [4:0] Write_Register,
  input  [31:0] Write_Data,
  input  Write,
  output [31:0] Read_Data_1,
  output [31:0] Read_Data_2
);

  wire decoder_1_out1, decoder_1_out2, decoder_1_out3, decoder_1_out4, decoder_1_out5, decoder_1_out6,
       decoder_1_out7, decoder_1_out8, decoder_1_out9, decoder_1_out10, decoder_1_out11, decoder_1_out12,
       decoder_1_out13, decoder_1_out14, decoder_1_out15, decoder_1_out16, decoder_1_out17, decoder_1_out18,
       decoder_1_out19, decoder_1_out20, decoder_1_out21, decoder_1_out22, decoder_1_out23, decoder_1_out24,
       decoder_1_out25, decoder_1_out26, decoder_1_out27, decoder_1_out28, decoder_1_out29, decoder_1_out30,
       decoder_1_out31;
  wire [31:0] delayer1x32_1_out, multiplexer_1_out, multiplexer_2_out, R1_q, R2_q, R3_q, R4_q, R5_q, R6_q,
       R7_q, R8_q, R9_q, R10_q, R11_q, R12_q, R13_q, R14_q, R15_q, R16_q, R17_q, R18_q, R19_q, R20_q, R21_q,
       R22_q, R23_q, R24_q, R25_q, R26_q, R27_q, R28_q, R29_q, R30_q, R31_q;

  Decoder #(.select(5), .disabled(0)) decoder_1 (
    .out1(decoder_1_out1), .out2(decoder_1_out2), .out3(decoder_1_out3), .out4(decoder_1_out4),
    .out5(decoder_1_out5), .out6(decoder_1_out6), .out7(decoder_1_out7), .out8(decoder_1_out8),
    .out9(decoder_1_out9), .out10(decoder_1_out10), .out11(decoder_1_out11), .out12(decoder_1_out12),
    .out13(decoder_1_out13), .out14(decoder_1_out14), .out15(decoder_1_out15), .out16(decoder_1_out16),
    .out17(decoder_1_out17), .out18(decoder_1_out18), .out19(decoder_1_out19), .out20(decoder_1_out20),
    .out21(decoder_1_out21), .out22(decoder_1_out22), .out23(decoder_1_out23), .out24(decoder_1_out24),
    .out25(decoder_1_out25), .out26(decoder_1_out26), .out27(decoder_1_out27), .out28(decoder_1_out28),
    .out29(decoder_1_out29), .out30(decoder_1_out30), .out31(decoder_1_out31), .sel(Write_Register),
    .en(Write));  // open: out0
  Delayer1x32 delayer1x32_1 (.in(Write_Data), .out(delayer1x32_1_out));
  Register #(.width(32)) R1 (.D(delayer1x32_1_out), .en(decoder_1_out1), .Q(R1_q), .clk(clk), .clr(reset));
  Register #(.width(32)) R2 (.D(delayer1x32_1_out), .en(decoder_1_out2), .Q(R2_q), .clk(clk), .clr(reset));
  Register #(.width(32)) R3 (.D(delayer1x32_1_out), .en(decoder_1_out3), .Q(R3_q), .clk(clk), .clr(reset));
  Register #(.width(32)) R4 (.D(delayer1x32_1_out), .en(decoder_1_out4), .Q(R4_q), .clk(clk), .clr(reset));
  Register #(.width(32)) R5 (.D(delayer1x32_1_out), .en(decoder_1_out5), .Q(R5_q), .clk(clk), .clr(reset));
  Register #(.width(32)) R6 (.D(delayer1x32_1_out), .en(decoder_1_out6), .Q(R6_q), .clk(clk), .clr(reset));
  Register #(.width(32)) R7 (.D(delayer1x32_1_out), .en(decoder_1_out7), .Q(R7_q), .clk(clk), .clr(reset));
  Register #(.width(32)) R8 (.D(delayer1x32_1_out), .en(decoder_1_out8), .Q(R8_q), .clk(clk), .clr(reset));
  Register #(.width(32)) R9 (.D(delayer1x32_1_out), .en(decoder_1_out9), .Q(R9_q), .clk(clk), .clr(reset));
  Register #(.width(32)) R10 (.D(delayer1x32_1_out), .en(decoder_1_out10), .Q(R10_q), .clk(clk), .clr(reset));
  Register #(.width(32)) R11 (.D(delayer1x32_1_out), .en(decoder_1_out11), .Q(R11_q), .clk(clk), .clr(reset));
  Register #(.width(32)) R12 (.D(delayer1x32_1_out), .en(decoder_1_out12), .Q(R12_q), .clk(clk), .clr(reset));
  Register #(.width(32)) R13 (.D(delayer1x32_1_out), .en(decoder_1_out13), .Q(R13_q), .clk(clk), .clr(reset));
  Register #(.width(32)) R14 (.D(delayer1x32_1_out), .en(decoder_1_out14), .Q(R14_q), .clk(clk), .clr(reset));
  Register #(.width(32)) R15 (.D(delayer1x32_1_out), .en(decoder_1_out15), .Q(R15_q), .clk(clk), .clr(reset));
  Register #(.width(32)) R16 (.D(delayer1x32_1_out), .en(decoder_1_out16), .Q(R16_q), .clk(clk), .clr(reset));
  Register #(.width(32)) R17 (.D(delayer1x32_1_out), .en(decoder_1_out17), .Q(R17_q), .clk(clk), .clr(reset));
  Register #(.width(32)) R18 (.D(delayer1x32_1_out), .en(decoder_1_out18), .Q(R18_q), .clk(clk), .clr(reset));
  Register #(.width(32)) R19 (.D(delayer1x32_1_out), .en(decoder_1_out19), .Q(R19_q), .clk(clk), .clr(reset));
  Register #(.width(32)) R20 (.D(delayer1x32_1_out), .en(decoder_1_out20), .Q(R20_q), .clk(clk), .clr(reset));
  Register #(.width(32)) R21 (.D(delayer1x32_1_out), .en(decoder_1_out21), .Q(R21_q), .clk(clk), .clr(reset));
  Register #(.width(32)) R22 (.D(delayer1x32_1_out), .en(decoder_1_out22), .Q(R22_q), .clk(clk), .clr(reset));
  Register #(.width(32)) R23 (.D(delayer1x32_1_out), .en(decoder_1_out23), .Q(R23_q), .clk(clk), .clr(reset));
  Register #(.width(32)) R24 (.D(delayer1x32_1_out), .en(decoder_1_out24), .Q(R24_q), .clk(clk), .clr(reset));
  Register #(.width(32)) R25 (.D(delayer1x32_1_out), .en(decoder_1_out25), .Q(R25_q), .clk(clk), .clr(reset));
  Register #(.width(32)) R26 (.D(delayer1x32_1_out), .en(decoder_1_out26), .Q(R26_q), .clk(clk), .clr(reset));
  Register #(.width(32)) R27 (.D(delayer1x32_1_out), .en(decoder_1_out27), .Q(R27_q), .clk(clk), .clr(reset));
  Register #(.width(32)) R28 (.D(delayer1x32_1_out), .en(decoder_1_out28), .Q(R28_q), .clk(clk), .clr(reset));
  Register #(.width(32)) R29 (.D(delayer1x32_1_out), .en(decoder_1_out29), .Q(R29_q), .clk(clk), .clr(reset));
  Register #(.width(32)) R30 (.D(delayer1x32_1_out), .en(decoder_1_out30), .Q(R30_q), .clk(clk), .clr(reset));
  Register #(.width(32)) R31 (.D(delayer1x32_1_out), .en(decoder_1_out31), .Q(R31_q), .clk(clk), .clr(reset));
  Multiplexer #(.select(5), .width(32), .enable("false")) multiplexer_1 (
    .in0({32{1'b0}}), .in1(R1_q), .in2(R2_q), .in3(R3_q), .in4(R4_q), .in5(R5_q), .in6(R6_q), .in7(R7_q),
    .in8(R8_q), .in9(R9_q), .in10(R10_q), .in11(R11_q), .in12(R12_q), .in13(R13_q), .in14(R14_q),
    .in15(R15_q), .in16(R16_q), .in17(R17_q), .in18(R18_q), .in19(R19_q), .in20(R20_q), .in21(R21_q),
    .in22(R22_q), .in23(R23_q), .in24(R24_q), .in25(R25_q), .in26(R26_q), .in27(R27_q), .in28(R28_q),
    .in29(R29_q), .in30(R30_q), .in31(R31_q), .out(multiplexer_1_out), .sel(Read_Register_1));
  Multiplexer #(.select(5), .width(32), .enable("false")) multiplexer_2 (
    .in0({32{1'b0}}), .in1(R1_q), .in2(R2_q), .in3(R3_q), .in4(R4_q), .in5(R5_q), .in6(R6_q), .in7(R7_q),
    .in8(R8_q), .in9(R9_q), .in10(R10_q), .in11(R11_q), .in12(R12_q), .in13(R13_q), .in14(R14_q),
    .in15(R15_q), .in16(R16_q), .in17(R17_q), .in18(R18_q), .in19(R19_q), .in20(R20_q), .in21(R21_q),
    .in22(R22_q), .in23(R23_q), .in24(R24_q), .in25(R25_q), .in26(R26_q), .in27(R27_q), .in28(R28_q),
    .in29(R29_q), .in30(R30_q), .in31(R31_q), .out(multiplexer_2_out), .sel(Read_Register_2));
  Delayer1x32 delayer1x32_2 (.in(multiplexer_1_out), .out(Read_Data_1));
  Delayer1x32 delayer1x32_3 (.in(multiplexer_2_out), .out(Read_Data_2));
endmodule

module ALU (
  input  [3:0] Operation,
  input  [31:0] A,
  input  [31:0] B,
  output Z,
  output [31:0] Result
);

  wire nor_1_out;
  wire [0:0] comparator_1_lt;
  wire [31:0] adder_1_out, and_1_out, multiplexer_1_out, multiplexer_2_out, multiplexer_3_out, not_1_out,
       not_2_out, or_1_out;

  assign not_1_out = ~A;  // NOT_Gate not_1, 32 bits wide
  assign not_2_out = ~B;  // NOT_Gate not_2, 32 bits wide
  Comparator #(.width(32)) comparator_1 (.a(A), .b(B), .lt(comparator_1_lt[0]));  // open: gt, eq
  Multiplexer #(.width(32), .enable("false")) multiplexer_1 (
    .in0(A), .in1(not_1_out), .out(multiplexer_1_out), .sel(Operation[3]));
  Multiplexer #(.width(32), .enable("false")) multiplexer_2 (
    .in0(B), .in1(not_2_out), .out(multiplexer_2_out), .sel(Operation[2]));
  assign and_1_out = multiplexer_1_out & multiplexer_2_out;  // AND_Gate and_1, 32 bits wide
  assign or_1_out = multiplexer_1_out | multiplexer_2_out;  // OR_Gate or_1, 32 bits wide
  Adder #(.width(32)) adder_1 (
    .a(multiplexer_1_out), .b(multiplexer_2_out), .out(adder_1_out), .cin(Operation[2]));  // open: cout
  Multiplexer #(.select(2), .width(32), .enable("false")) multiplexer_3 (
    .in0(and_1_out), .in1(or_1_out), .in2(adder_1_out), .in3({{31{1'b0}}, comparator_1_lt[0]}),
    .out(multiplexer_3_out), .sel(Operation[1:0]));
  nor nor_1 (nor_1_out, multiplexer_3_out[0], multiplexer_3_out[1], multiplexer_3_out[2], multiplexer_3_out[3], multiplexer_3_out[4], multiplexer_3_out[5], multiplexer_3_out[6], multiplexer_3_out[7], multiplexer_3_out[8], multiplexer_3_out[9], multiplexer_3_out[10], multiplexer_3_out[11], multiplexer_3_out[12], multiplexer_3_out[13], multiplexer_3_out[14], multiplexer_3_out[15], multiplexer_3_out[16], multiplexer_3_out[17], multiplexer_3_out[18], multiplexer_3_out[19], multiplexer_3_out[20], multiplexer_3_out[21], multiplexer_3_out[22], multiplexer_3_out[23], multiplexer_3_out[24], multiplexer_3_out[25], multiplexer_3_out[26], multiplexer_3_out[27], multiplexer_3_out[28], multiplexer_3_out[29], multiplexer_3_out[30], multiplexer_3_out[31]);
  Delayer2x32 delayer2x32_1 (.in(multiplexer_3_out), .out(Result));
  Delayer2x1 delayer2x1_1 (.in(nor_1_out), .out(Z));

  // Notes on the sheet:
  //   0001    OR
  //   Operation    Function
  //   0000    AND
  //   0010    add
  //   0110    subtract
  //   0111    set on less than
  //   1100    NOR
endmodule

module Data_Memory_32 (
  input  Write,
  input  [31:0] Address,
  input  [31:0] Write_Data,
  input  clk,
  input  reset,
  input  Read,
  output [31:0] Read_Data
);

  wire [9:0] bitselector_1_out;
  wire [31:0] delayer2x32_1_out, ram_1_data;

  BitSelector #(.width(32), .group(10)) bitselector_1 (.in(Address), .out(bitselector_1_out), .sel(2'b00));
  Delayer2x32 delayer2x32_1 (.in(Write_Data), .out(delayer2x32_1_out));
  RAM #(.dataWidth(32), .bus("separate"), .Datafile_on_reset("TG00ram.txt")) ram_1 (
    .addr(bitselector_1_out[9:2]), .din(delayer2x32_1_out), .data(ram_1_data), .str(Write), .sel(1'b1),
    .clk(clk), .ld(Read), .clr(reset));
  Delayer2x32 delayer2x32_2 (.in(ram_1_data), .out(Read_Data));

  // Notes on the sheet:
  //   Memoria de 32 bits direccionable a nivel de byte
  //   Tan solo implementadas las 256 primeras posiciones de 32 bits o 1024 bytes
endmodule

module Instruction_memory (
  input  [31:0] Read_address,
  output [31:0] Instruction
);

  wire [6:0] bitselector_1_out;
  wire [31:0] ram_1_data;

  BitSelector #(.width(30), .group(7)) bitselector_1 (.in(Read_address[31:2]), .out(bitselector_1_out), .sel(3'b000));
  RAM #(.addrWidth(7), .dataWidth(32), .bus("asynch"), .Datafile_on_reset("TG00rom.txt")) ram_1 (
    .addr(bitselector_1_out), .data(ram_1_data), .sel(1'b1), .ld(1'b1), .clr(1'b0));
  Delayer2x32 delayer2x32_1 (.in(ram_1_data), .out(Instruction));
endmodule

module InstDecoder (
  input  [31:0] IB,
  output [5:0] IB31_26__opc,
  output [4:0] IB25_21__rs,
  output [4:0] IB20_16__rt,
  output [4:0] IB15_11__rd,
  output [5:0] IB5_0__func,
  output [15:0] IB15_0__imm,
  output [25:0] IB25_0__addr
);


  assign IB5_0__func = IB[5:0];
  assign IB15_0__imm = IB[15:0];
  assign IB15_11__rd = IB[15:11];
  assign IB20_16__rt = IB[20:16];
  assign IB25_0__addr = IB[25:0];
  assign IB25_21__rs = IB[25:21];
  assign IB31_26__opc = IB[31:26];
endmodule

module Control_ALU (
  input  [1:0] OpALU,
  input  [5:0] funcion,
  output [3:0] OUT
);

  wire [3:0] multiplexer_1_out;

  Multiplexer #(.select(4), .width(4), .enable("false")) multiplexer_1 (
    .in0(4'b0010), .in2(4'b0110), .in4(4'b0000), .in5(4'b0001), .in10(4'b0111), .out(multiplexer_1_out),
    .sel(funcion[3:0]));  // open: in1, in3, in6, in7, in8, in9, in11, in12, in13, in14, in15
  Multiplexer #(.select(2), .width(4), .enable("false")) multiplexer_2 (
    .in0(4'b0010), .in1(4'b0110), .in2(multiplexer_1_out), .out(OUT), .sel(OpALU));  // open: in3
endmodule

module ControlUnit (
  input  [5:0] OPC,
  output JUMP,
  output HALT,
  output FC,
  output WR,
  output RM,
  output MpxR,
  output WM,
  output FB,
  output AluOp0,
  output AluOp1
);

  wire ADDI_out, not_1_out;

  Control_ALU control_alu_1 ();  // open: OpALU, funcion, OUT
  and u_JUMP (JUMP, ~OPC[0], OPC[1], ~OPC[2], ~OPC[3], ~OPC[4], ~OPC[5]);  // AND_Gate
  and ADDI (ADDI_out, ~OPC[0], ~OPC[1], ~OPC[2], OPC[3], ~OPC[4], ~OPC[5]);  // AND_Gate
  and LW (RM, OPC[0], OPC[1], ~OPC[2], ~OPC[3], ~OPC[4], OPC[5]);  // AND_Gate
  and SW (WM, OPC[0], OPC[1], ~OPC[2], OPC[3], ~OPC[4], OPC[5]);  // AND_Gate
  and BEQ (AluOp0, ~OPC[0], ~OPC[1], OPC[2], ~OPC[3], ~OPC[4], ~OPC[5]);  // AND_Gate
  and R (AluOp1, ~OPC[0], ~OPC[1], ~OPC[2], ~OPC[3], ~OPC[4], ~OPC[5]);  // AND_Gate
  and u_HALT (HALT, OPC[0], OPC[1], OPC[2], OPC[3], OPC[4], OPC[5]);
  not not_1 (not_1_out, ADDI_out);
  or or_1 (WR, ADDI_out, AluOp1, RM);
  or or_2 (MpxR, ADDI_out, RM);
  or or_3 (FB, AluOp0, AluOp1);
  xor xor_1 (FC, AluOp1, not_1_out);
endmodule
