// Logisim project Delayer.circ as structural Verilog: 5 circuits, main circuit Delayer2x32
module Delayer2x32 (
  input  [31:0] in,
  output [31:0] out
);

  wire clock_1_out;
  wire [31:0] register_1_q;

  Clock clock_1 (.out(clock_1_out));
  Register #(.width(32)) register_1 (.D(in), .Q(register_1_q), .clk(clock_1_out));  // open: en, clr
  Register #(.width(32)) register_2 (.D(register_1_q), .Q(out), .clk(clock_1_out));  // open: en, clr
endmodule

module Delayer1x32 (
  input  [31:0] in,
  output [31:0] out
);

  wire clock_1_out;

  Clock clock_1 (.out(clock_1_out));
  Register #(.width(32)) register_1 (.D(in), .Q(out), .clk(clock_1_out));  // open: en, clr
endmodule

module Delayer2x1 (
  input  in,
  output out
);

  wire clock_1_out, register_1_q;

  Clock clock_1 (.out(clock_1_out));
  Register #(.width(1)) register_1 (.D(in), .Q(register_1_q), .clk(clock_1_out));  // open: en, clr
  Register #(.width(1)) register_2 (.D(register_1_q), .Q(out), .clk(clock_1_out));  // open: en, clr
endmodule

module StopClk (
  input  halt,
  input  clkin,
  output clkout
);

  wire d_ff_1_q, not_1_out, TickClk_out;
  wire [31:0] adder_1_out, counter_1_q, counter_2_q, counter_3_q;

  Clock TickClk (.out(TickClk_out));
  D_Flip_Flop d_ff_1 (.clk(halt), .D(halt), .Q(d_ff_1_q));  // open: Qn, preset, en, reset
  not not_1 (not_1_out, clkin);
  Counter #(.width(32), .max('hffffffff)) counter_1 (
    .Q(counter_1_q), .clk(TickClk_out));  // open: load, D, count, carry, clr
  Counter #(.width(32), .max('hffffffff), .trigger("falling")) counter_2 (
    .Q(counter_2_q), .clk(TickClk_out));  // open: load, D, count, carry, clr
  or or_1 (clkout, d_ff_1_q, not_1_out);
  Adder #(.width(32)) adder_1 (.a(counter_1_q), .b(counter_2_q), .out(adder_1_out));  // open: cin, cout
  Counter #(.width(32), .max('hffffffff)) counter_3 (
    .Q(counter_3_q), .clk(clkout));  // open: load, D, count, carry, clr
  // Probe on counter_3_q
  // Probe on adder_1_out
endmodule

module clock_divider (
  input  clk_in,
  output clk,
  output clk_2,
  output clk_4,
  output clk_8,
  output clk_16,
  output clk_32
);

  Counter #(.width(5), .max('h1f)) counter_1 (
    .Q({clk_32, clk_16, clk_8, clk_4, clk_2}), .clk(clk_in));  // open: load, D, count, carry, clr

  assign clk = clk_in;
endmodule
