// Logisim project Z23_examen.circ as structural Verilog: 8 circuits, main circuit Main
module Main (
  output [7:0] OUT
);

  wire C_Unit_halt, C_Unit_imty, C_Unit_mw, C_Unit_rsource, C_Unit_rw, C_Unit_wa, clock_1_out, Decod_rd,
       Decod_rs, nor_1_out, RESET_out;
  wire [2:0] Decod_func, Decod_opc;
  wire [5:0] Decod_addr;
  wire [7:0] B__Registros_a_2, B__Registros_b_2, Decod_imm, M__Datos_out, multiplexer_1_out,
       multiplexer_2_out;
  wire [15:0] M__Instruccion_out;

  Button RESET (.out(RESET_out));
  Memoria_de_Instruccion M__Instruccion (
    .addr(Decod_addr), .out(M__Instruccion_out), .WA(C_Unit_wa), .clk(nor_1_out), .reset(RESET_out),
    .R0(B__Registros_a_2), .R1(B__Registros_b_2));
  nor nor_1 (nor_1_out, C_Unit_halt, clock_1_out);
  Clock clock_1 (.out(clock_1_out));
  Multiplexer #(.width(8)) multiplexer_1 (
    .in0(OUT), .in1(M__Datos_out), .out(multiplexer_1_out), .sel(C_Unit_rsource));  // open: en
  // Probe on M__Instruccion_out
  Banco_de_Registros B__Registros (
    .IN(multiplexer_1_out), .C(Decod_rd), .WR(C_Unit_rw), .CLK(nor_1_out), .clear(RESET_out), .A(Decod_rd),
    .B(Decod_rs), .A_2(B__Registros_a_2), .B_2(B__Registros_b_2));
  Decodificador Decod (
    .in_1(M__Instruccion_out), .addr(Decod_addr), .imm(Decod_imm), .func(Decod_func), .rs(Decod_rs),
    .rd(Decod_rd), .opc(Decod_opc));
  Multiplexer #(.width(8)) multiplexer_2 (
    .in0(B__Registros_a_2), .in1(Decod_imm), .out(multiplexer_2_out), .sel(C_Unit_imty));  // open: en
  ALU ALU (.A(B__Registros_b_2), .B(multiplexer_2_out), .Func(Decod_func), .salida(OUT));
  Unidad_de_control C_Unit (
    .opc(Decod_opc), .RW(C_Unit_rw), .imty(C_Unit_imty), .MW(C_Unit_mw), .Rsource(C_Unit_rsource),
    .halt(C_Unit_halt), .WA(C_Unit_wa));
  Memoria_de_Datos M__Datos (
    .ADDR(Decod_addr), .IN(B__Registros_a_2), .MW(C_Unit_mw), .CLK(nor_1_out), .OUT(M__Datos_out));
endmodule

module Banco_de_Registros (
  input  [7:0] IN,
  input  C,
  input  WR,
  input  B,
  input  CLK,
  input  A,
  input  clear,
  output [7:0] A_2,
  output [7:0] B_2
);

  wire and_1_out, multiplexer_1_out;
  wire [7:0] demultiplexer_1_out0, demultiplexer_1_out1, R0_q, R1_q;

  Demultiplexer #(.width(8), .enable("false")) demultiplexer_1 (
    .out0(demultiplexer_1_out0), .out1(demultiplexer_1_out1), .in(IN), .sel(C));
  Multiplexer #(.select(2), .enable("false")) multiplexer_1 (
    .in0(1'b0), .in1(1'b0), .in2(1'b1), .in3(1'b0), .out(multiplexer_1_out), .sel({WR, C}));
  and and_1 (and_1_out, C, WR);
  // Probe on R0_q
  Register R0 (.D(demultiplexer_1_out0), .en(multiplexer_1_out), .Q(R0_q), .clk(CLK), .clr(clear));
  Register R1 (.D(demultiplexer_1_out1), .en(and_1_out), .Q(R1_q), .clk(CLK), .clr(clear));
  // Probe on R1_q
  Multiplexer #(.width(8), .enable("false")) multiplexer_2 (.in0(R0_q), .in1(R1_q), .out(A_2), .sel(A));
  Multiplexer #(.width(8), .enable("false")) multiplexer_3 (.in0(R0_q), .in1(R1_q), .out(B_2), .sel(B));
endmodule

module Memoria_de_Datos (
  input  [5:0] ADDR,
  input  [7:0] IN,
  input  MW,
  input  CLK,
  output [7:0] OUT
);

  RAM #(.addrWidth(6), .bus("separate"), .Datafile_on_reset("data.txt")) ram_1 (
    .addr(ADDR), .din(IN), .data(OUT), .str(MW), .clk(CLK), .ld(1'b1));  // open: sel, clr
endmodule

module Memoria_de_Instruccion (
  input  [5:0] addr,
  input  WA,
  input  clk,
  input  reset,
  input  [7:0] R0,
  input  [7:0] R1,
  output [15:0] out
);

  wire and_1_out, comparator_1_eq, not_1_out;
  wire [5:0] adder_1_out, multiplexer_1_out, PC_q;
  wire [7:0] alu_1_salida;

  ALU alu_1 (.A(R0), .B(R1), .Func(3'b101), .salida(alu_1_salida));
  not not_1 (not_1_out, comparator_1_eq);
  Comparator comparator_1 (.a(alu_1_salida), .b(8'h1), .eq(comparator_1_eq));  // open: gt, lt
  Multiplexer #(.width(6)) multiplexer_1 (
    .in0(adder_1_out), .in1(addr), .out(multiplexer_1_out), .sel(and_1_out));  // open: en
  and and_1 (and_1_out, WA, not_1_out);
  Register #(.width(6)) PC (.D(multiplexer_1_out), .Q(PC_q), .clk(clk), .clr(reset));  // open: en
  Adder #(.width(6)) adder_1 (.a(6'b000001), .b(PC_q), .out(adder_1_out));  // open: cin, cout
  RAM #(.addrWidth(6), .dataWidth(16), .Datafile_on_reset("memoria.txt")) ram_1 (
    .addr(PC_q), .data(out), .clk(clk), .clr(reset));  // open: sel, ld
endmodule

module Unidad_de_control (
  input  [2:0] opc,
  output RW,
  output imty,
  output MW,
  output Rsource,
  output halt,
  output WA
);

  wire and_3_out, and_4_out, not_1_out, not_2_out, not_4_out, not_5_out, not_6_out, not_7_out;

  not not_1 (not_1_out, opc[2]);
  not not_2 (not_2_out, opc[2]);
  not not_3 (imty, opc[1]);
  not not_4 (not_4_out, opc[2]);
  not not_5 (not_5_out, opc[1]);
  not not_6 (not_6_out, opc[0]);
  and and_1 (Rsource, opc[1], opc[0]);
  and and_2 (halt, opc[2], opc[1]);
  not not_7 (not_7_out, opc[1]);
  and and_3 (and_3_out, not_1_out, opc[0]);
  or or_1 (RW, and_3_out, and_4_out);
  and and_4 (and_4_out, not_2_out, opc[1]);
  and and_5 (MW, not_4_out, not_5_out, not_6_out);
  and and_6 (WA, opc[2], not_7_out);
endmodule

module Decodificador (
  input  [15:0] in_1,
  output [5:0] addr,
  output [7:0] imm,
  output [2:0] func,
  output rs,
  output rd,
  output [2:0] opc
);


  assign addr = in_1[5:0];
  assign func = in_1[10:8];
  assign imm = in_1[7:0];
  assign opc = in_1[15:13];
  assign rd = in_1[12];
  assign rs = in_1[11];

  // Notes on the sheet:
  //   7 bits
endmodule

module ALU (
  input  [7:0] A,
  input  [7:0] B,
  input  [2:0] Func,
  output [7:0] salida
);

  wire comparator_1_gt;
  wire [7:0] adder_1_out, div, divider_1_rem, multiplexer_1_out, multiplier_1_out, subtractor_1_out;

  Adder adder_1 (.a(A), .b(B), .out(adder_1_out));  // open: cin, cout
  Subtractor subtractor_1 (.a(A), .b(B), .out(subtractor_1_out));  // open: bin, bout
  Multiplier multiplier_1 (.a(A), .b(B), .out(multiplier_1_out));  // open: cin, cout
  Divider divider_1 (.a(A), .b(B), .rem(divider_1_rem));  // open: out, upper
  Comparator comparator_1 (.a(A), .b(B), .gt(comparator_1_gt));  // open: eq, lt
  Division division_1 (.A(A), .B(B), .out_3(div));
  Multiplexer #(.width(8)) multiplexer_1 (
    .in0(A), .in1(B), .out(multiplexer_1_out), .sel(comparator_1_gt));  // open: en
  Multiplexer #(.select(3), .width(8)) multiplexer_2 (
    .in0(A), .in1(B), .in2(adder_1_out), .in3(subtractor_1_out), .in4(multiplier_1_out), .in5(div),
    .in6(divider_1_rem), .in7(multiplexer_1_out), .out(salida), .sel(Func));  // open: en
endmodule

module Division (
  input  [7:0] A,
  input  [7:0] B,
  output [7:0] out_3
);

  wire comparator_1_eq, comparator_2_eq, xor_1_out;
  wire [2:0] bitfinder_1_index, bitfinder_2_index;
  wire [7:0] divider_1_out, multiplexer_1_out, multiplexer_2_out, negator_1_out, negator_2_out, negator_3_out;

  BitFinder #(.\type ("high1")) bitfinder_1 (.in(A), .index(bitfinder_1_index));  // open: found
  BitFinder #(.\type ("high1")) bitfinder_2 (.in(B), .index(bitfinder_2_index));  // open: found
  Negator negator_1 (.in(A), .out(negator_1_out));
  Comparator #(.width(3)) comparator_1 (.a(bitfinder_1_index), .b(3'b111), .eq(comparator_1_eq));  // open: gt, lt
  Negator negator_2 (.in(B), .out(negator_2_out));
  Comparator #(.width(3)) comparator_2 (.a(bitfinder_2_index), .b(3'b111), .eq(comparator_2_eq));  // open: gt, lt
  Multiplexer #(.width(8), .enable("false")) multiplexer_1 (
    .in0(A), .in1(negator_1_out), .out(multiplexer_1_out), .sel(comparator_1_eq));
  Multiplexer #(.width(8), .enable("false")) multiplexer_2 (
    .in0(B), .in1(negator_2_out), .out(multiplexer_2_out), .sel(comparator_2_eq));
  Divider divider_1 (.a(multiplexer_1_out), .b(multiplexer_2_out), .out(divider_1_out));  // open: upper, rem
  Negator negator_3 (.in(divider_1_out), .out(negator_3_out));
  xor xor_1 (xor_1_out, comparator_1_eq, comparator_2_eq);
  Multiplexer #(.width(8)) multiplexer_3 (
    .in0(divider_1_out), .in1(negator_3_out), .out(out_3), .sel(xor_1_out));  // open: en

  // Notes on the sheet:
  //   Realiza la división en valor absoluto evitando problemas con numeros negativos
endmodule
