// Logisim project fibonacci.circ as structural Verilog: 2 circuits, main circuit main
module main (
  input  [3:0] n,
  output [5:0] fibonacci_n
);

  wire fibonacci_1_halt, fibonacci_1_running, Reset_out;

  Button Reset (.out(Reset_out));
  fibonacci fibonacci_1 (
    .Input(n), .Reset(Reset_out), .Halt(fibonacci_1_halt), .fibonacci_n(fibonacci_n),
    .Running(fibonacci_1_running));
  LED Finish (.in(fibonacci_1_halt));
  LED Running (.in(fibonacci_1_running));
  // Probe on fibonacci_n
endmodule

module fibonacci (
  input  [3:0] Input,
  input  Reset,
  output Halt,
  output [5:0] fibonacci_n,
  output Running
);

  wire CLK_out, comparator_1_eq, comparator_2_eq, comparator_2_gt, d_ff_1_q, or_1_out;
  wire [3:0] adder_1_out, counter_1_q;
  wire [5:0] adder_2_out, multiplexer_1_out, register_2_q;

  Clock CLK (.out(CLK_out));
  Counter #(.width(4), .max('hf), .ongoal("stay")) counter_1 (
    .D(adder_1_out), .Q(counter_1_q), .clk(CLK_out), .clr(Reset));  // open: load, count, carry
  Comparator #(.width(4), .mode("unsigned")) comparator_1 (
    .a(counter_1_q), .b(4'b0001), .eq(comparator_1_eq));  // open: gt, lt
  Multiplexer #(.width(6)) multiplexer_1 (
    .in0(adder_2_out), .in1(6'b000001), .out(multiplexer_1_out), .sel(comparator_1_eq));  // open: en
  D_Flip_Flop d_ff_1 (.clk(CLK_out), .D(1'b1), .Q(d_ff_1_q), .preset(Reset), .en(1'b1), .reset(Reset));  // open: Qn
  Adder #(.width(4)) adder_1 (.a(4'b0001), .b(counter_1_q), .out(adder_1_out));  // open: cin, cout
  Register #(.width(6)) register_1 (.D(multiplexer_1_out), .en(or_1_out), .Q(fibonacci_n), .clk(CLK_out), .clr(Reset));
  Register #(.width(6)) register_2 (.D(fibonacci_n), .en(or_1_out), .Q(register_2_q), .clk(CLK_out), .clr(Reset));
  xor xor_1 (Running, Halt, d_ff_1_q);
  Comparator #(.width(4), .mode("unsigned")) comparator_2 (
    .a(Input), .b(counter_1_q), .gt(comparator_2_gt), .eq(comparator_2_eq), .lt(Halt));
  or or_1 (or_1_out, comparator_2_eq, comparator_2_gt);
  Adder #(.width(6)) adder_2 (.a(fibonacci_n), .b(register_2_q), .out(adder_2_out));  // open: cin, cout

  // Notes on the sheet:
  //   Halt: pull=up
  //   Running: pull=up
endmodule
